// Logisim project Beaver-Lab1.circ as structural Verilog: 1 circuit, main circuit main
module main (
  input  A,
  input  B,
  input  C,
  input  D,
  output D1,
  output D2
);

  wire _01X1_out, _0100_out, _0111_out, _1110_out, A_prime_out, C_prime_out, D_prime_out, NOT_out;

  nand D_prime (D_prime_out, D, D);
  nand A_prime (A_prime_out, A, A);
  nand C_prime (C_prime_out, C, C);
  nand _1110 (_1110_out, A, B, C, D_prime_out);
  nand _01X1 (_01X1_out, A_prime_out, B, D);
  nand _0100 (_0100_out, A_prime_out, B, C_prime_out, D_prime_out);
  nand NOT (NOT_out, _01X1_out, _01X1_out);
  nand _0111 (_0111_out, NOT_out, C);
  nand OR__D1 (D1, _1110_out, _01X1_out);
  nand OR__D2 (D2, _0111_out, _0100_out);

  // Notes on the sheet:
  //   Inputs
  //   |____________|
  //   Complements
  //   |________________________________|
  //   First Layer NAND
  //   |________|
  //   Outputs
  //   Second Layer NAND
endmodule
