// Logisim project Beaver-Lab2Part1.circ as structural Verilog: 1 circuit, main circuit main
module main (
  input  S1,
  input  S0,
  input  _1_0,
  input  _1_1,
  input  _1_2,
  input  _1_3,
  input  _2_0,
  input  _2_1,
  input  _2_2,
  input  _2_3,
  output _1,
  output _2
);

  wire and_1_out, and_2_out, and_3_out, and_4_out, and_5_out, and_6_out, and_7_out, and_8_out, not_1_out,
       not_2_out;

  not not_1 (not_1_out, S1);
  not not_2 (not_2_out, S0);
  and and_1 (and_1_out, _1_0, not_1_out, not_2_out);
  and and_2 (and_2_out, _1_1, not_1_out, S0);
  and and_3 (and_3_out, _1_2, S1, not_2_out);
  and and_4 (and_4_out, _1_3, S1, S0);
  and and_5 (and_5_out, _2_0, not_1_out, not_2_out);
  and and_6 (and_6_out, _2_1, not_1_out, S0);
  and and_7 (and_7_out, _2_2, S1, not_2_out);
  and and_8 (and_8_out, _2_3, S1, S0);
  or or_1 (_1, and_1_out, and_2_out, and_3_out, and_4_out);
  or or_2 (_2, and_5_out, and_6_out, and_7_out, and_8_out);

  // Notes on the sheet:
  //   Selection
endmodule
