// Logisim project Beaver-Lab2Part2.circ as structural Verilog: 1 circuit, main circuit main
module main (
  input  S1,
  input  S0,
  input  A,
  input  B,
  input  C,
  input  D,
  output D1,
  output D2
);

  wire _00_2_out, _00_out, _01_2_out, _01_out, _01X1_out, _10_2_out, _10_out, _11_2_out, _11_out, _0100_out,
       _0111_out, _1110_out, A_prime_out, C_prime_out, D_prime_out, not_2_out, not_3_out, NOT_out,
       OR__D1_out, OR__D2_out;

  nand D_prime (D_prime_out, D, D);
  nand A_prime (A_prime_out, A, A);
  nand C_prime (C_prime_out, C, C);
  nand _1110 (_1110_out, A, B, C, D_prime_out);
  nand _01X1 (_01X1_out, A_prime_out, B, D);
  nand _0100 (_0100_out, A_prime_out, B, C_prime_out, D_prime_out);
  nand NOT (NOT_out, _01X1_out, _01X1_out);
  nand _0111 (_0111_out, NOT_out, C);
  nand OR__D1 (OR__D1_out, _1110_out, _01X1_out);
  nand OR__D2 (OR__D2_out, _0111_out, _0100_out);
  not not_2 (not_2_out, S1);
  not not_3 (not_3_out, S0);
  and _00 (_00_out, OR__D1_out, not_2_out, not_3_out);
  and _01 (_01_out, OR__D1_out, not_2_out, S0);
  and _10 (_10_out, 1'b0, S1, not_3_out);
  and _11 (_11_out, 1'b0, S1, S0);
  and _00_2 (_00_2_out, OR__D2_out, not_2_out, not_3_out);
  and _01_2 (_01_2_out, 1'b0, not_2_out, S0);
  and _10_2 (_10_2_out, OR__D2_out, S1, not_3_out);
  and _11_2 (_11_2_out, 1'b0, S1, S0);
  or or_1 (D1, _00_out, _01_out, _10_out, _11_out);
  or or_2 (D2, _00_2_out, _01_2_out, _10_2_out, _11_2_out);

  // Notes on the sheet:
  //   Inputs
  //   |____________|
  //   Complements
  //   First Layer NAND
  //   |________________________________|
  //   |________|
  //   Second Layer NAND
  //   Selection
  //   Multiplexer
  //   |___________________________________________|
  //   Outputs
endmodule
