// Logisim project Beaver-Lab3.circ as structural Verilog: 1 circuit, main circuit main
module main (
  input  Serial_Input,
  output Output
);

  wire _0111_out, _1010_out, clock_1_out, d_ff_1_q, d_ff_2_q, d_ff_3_q, d_ff_4_q, not_1_out, not_2_out,
       not_3_out;

  Clock clock_1 (.out(clock_1_out));
  D_Flip_Flop d_ff_1 (.clk(clock_1_out), .D(Serial_Input), .Q(d_ff_1_q));  // open: Qn, preset, en, reset
  not not_1 (not_1_out, d_ff_1_q);
  D_Flip_Flop d_ff_2 (.clk(clock_1_out), .D(d_ff_1_q), .Q(d_ff_2_q));  // open: Qn, preset, en, reset
  not not_2 (not_2_out, d_ff_2_q);
  D_Flip_Flop d_ff_3 (.clk(clock_1_out), .D(d_ff_4_q), .Q(d_ff_3_q));  // open: Qn, preset, en, reset
  D_Flip_Flop d_ff_4 (.clk(clock_1_out), .D(d_ff_2_q), .Q(d_ff_4_q));  // open: Qn, preset, en, reset
  not not_3 (not_3_out, d_ff_3_q);
  and _0111 (_0111_out, not_1_out, d_ff_2_q, d_ff_4_q, d_ff_3_q);
  and _1010 (_1010_out, d_ff_1_q, not_2_out, d_ff_4_q, not_3_out);
  or or_1 (Output, _0111_out, _1010_out);

  // Notes on the sheet:
  //   Clock
endmodule
